# Fritzing sketch EspTempSensorDS18B20 (saved by Fritzing 0.9.3b)
circuit board: 3.04563cm x 1.63628cm
breadboards: 1

parts:
  R4 = Resistor [tolerance=±5% resistance=4.7k package="1206 [SMD]"]
  C2 = Tantalum Capacitor [capacitance=1μF package="B 3528 [SMD, tantalum]"]
  C1 = Tantalum Capacitor [capacitance=1μF package="B 3528 [SMD, tantalum]"]
  R3 = Resistor [tolerance=±5% resistance=10k package="1206 [SMD]"]
  R2 = Resistor [tolerance=±5% resistance=10k package="1206 [SMD]"]
  R1 = Resistor [tolerance=±5% resistance=10k package="1206 [SMD]"]
  HT7333 = TRANSISTOR_NPN [package=sot89]
  DS1 = DS18B20 1-Wire Temperature Sensor [part_number=DS18B20]
  ESP-1 = ESP-01 [part_number=ESP8266]
  J1 = double row male pin header, 2 pins [form="♂ (male)"]

nets:
  N1: R4.Pin_0, DS1.DQ, ESP-1.GPIO2
  VDD: R4.Pin_1, C1.+, R3.Pin_0, R2.Pin_1, R1.Pin_1, HT7333.B, DS1.VDD, ESP-1.VCC
  GND: C2.-, C1.-, HT7333.E, DS1.GND, ESP-1.GND, J1.pin2
  N2: C2.+, HT7333.C, J1.pin1
  N3: R3.Pin_1, ESP-1.GPIO0
  N4: R2.Pin_0, ESP-1.CH_PD
  N5: R1.Pin_0, ESP-1.RST

custom parts:
  ESP-01: ESP8266 Module, especifically the ESP-01.
